# Fritzing sketch Booster (saved by Fritzing 0.9.3b)
circuit board: 4.11884cm x 4.82058cm
breadboards: 1

parts:
  74HC14 = IC, DIP package, 14 pins [chip_label=3xNOT]
  R1 = Resistor [tolerance=±5% resistance=1k package=THT]
  R2 = Resistor [tolerance=±5% resistance=1k package=THT]
  +5V_IN_OUT_GND = screw terminal, 4 pins
  D1 = Rectifier Diode [part_number=1N4001 package="300 mil [THT]"]
  D2 = Rectifier Diode [part_number=1N4001 package="300 mil [THT]"]
  12V~ = screw terminal, 3 pins
  G1 = SKB B40 C1400 [package=G3]
  TLE_5205 = TLE 5205 H-Bridge [package=P-TO220-7-11]
  C2 = Electrolytic Capacitor [capacitance=4.7µF package="100 mil [THT, electrolytic]"]
  C3 = Electrolytic Capacitor [capacitance=4.7µF package="100 mil [THT, electrolytic]"]
  D3 = Rectifier Diode [part_number=1N4001 package="300 mil [THT]"]
  D4 = Rectifier Diode [part_number=1N4001 package="300 mil [THT]"]
  R3 = Resistor [tolerance=±5% resistance=10k package=THT]
  C1 = Electrolytic Capacitor [capacitance=1mF voltage=35V package="300 mil [THT, electrolytic]"]
  DCC = Screw terminal - 2 pins [package=THT]

nets:
  N1: 74HC14.pin1, 74HC14.pin3, +5V_IN_OUT_GND.pin3, TLE_5205.IN2
  N2: 74HC14.pin2, D1.anode
  N3: 74HC14.pin4, 74HC14.pin5
  N4: 74HC14.pin6, D2.anode
  GND: 74HC14.pin7, R1.Pin_0, R2.Pin_0, +5V_IN_OUT_GND.pin1, 12V~.pin3, G1.4, TLE_5205.GND, C2.-, C3.-, R3.Pin_0, C1.-
  N5: 74HC14.pin10, D4.anode
  N6: 74HC14.pin11, R2.Pin_1, D2.cathode, C3.+
  N7: 74HC14.pin12, D3.anode
  N8: 74HC14.pin13, R1.Pin_1, D1.cathode, C2.+
  N9: 74HC14.pin14, +5V_IN_OUT_GND.pin4
  N10: +5V_IN_OUT_GND.pin2, TLE_5205.EF
  N11: 12V~.pin1, G1.1
  N12: 12V~.pin2, G1.3
  N13: G1.2, TLE_5205.V_S, C1.+
  N14: TLE_5205.OUT1, DCC.pin1
  N15: TLE_5205.IN1, D3.cathode, D4.cathode, R3.Pin_1
  N16: TLE_5205.OUT2, DCC.pin2

notes:
  SRSoftware
  Booster v4
  EF
  GND
  V+
  1
  2

custom parts:
  TLE 5205 H-Bridge: The TLE 5205-2 is an integrated power H-bridge with DMOS output stages for driving DC-Motors. Operation modes forward (cw), reverse (ccw), brake and high impedance are invoked from just two control pins with TTL/CMOS compatible levels.
