# Fritzing sketch booster (saved by Fritzing 0.8.5b)
circuit board: 6.35418cm x 3.85608cm
breadboards: 1

parts:
  R5 = Resistor [tolerance=±5% resistance=22k package=THT]
  R4 = Resistor [tolerance=±5% resistance=2.2k package=THT]
  J1 = Screw terminal - 2 pins [package=THT]
  R1 = Resistor [tolerance=±5% resistance=22k package=THT]
  J2 = screw terminal, 4 pins
  C1 = SKB B40 C1400 [package=G3]
  5205 = TLE 5205-2S [package=TDO220]
  R3 = Resistor [tolerance=±5% resistance=2.2k package=THT]
  C2 = Electrolytic Capacitor [capacitance=0.47mF voltage=50V package="300 mil [THT, electrolytic]"]
  J3 = screw terminal, 2 pins
  Q1 = NPN-Transistor [package="TO92 [THT]"]
  R2 = Resistor [tolerance=±5% resistance=22k package=THT]

nets:
  N1: R5.Pin_0, J2.pin3, R2.Pin_0
  N2: R5.Pin_1, J2.pin1, 5205.2
  N3: R4.Pin_0, J2.pin2, Q1.B
  N4: R4.Pin_1, R1.Pin_0, 5205.5
  N5: J1.pin1, C1.1
  N6: J1.pin2, C1.3
  GND: R1.Pin_1, J2.pin4, C1.4, 5205.4, R3.Pin_1, C2.-
  N7: C1.2, 5205.6, C2.+
  N8: 5205.1, J3.pin2
  N9: 5205.3, Q1.C, R2.Pin_1
  N10: 5205.7, J3.pin1
  N11: R3.Pin_0, Q1.E
